# Fritzing sketch station-proto (saved by Fritzing 0.9.10b)
breadboards: 1

parts:
  Raspberry_Pi_1 = Raspberry Pi 3 [part_number=RPI-3-V1.2]
  2_Channel_Relay1 = 2 Channel Power Relay
  TXS0108E_8-Bit_Bi-directional_Level-Shifting_Voltage_Translator1 = TXS0108 [part_number=TXS0108EPW package=TSSOP]  # not connected
  R1 = Resistor [tolerance=±5% power=0.25 resistance=1k package=THT]
  Part1 = LCD1602-I2C
  U1 = RFID RC522 SIP - 8 pins [chip_label="RFID RC522" package="SIP (Single Inline) [THT]"]
  M1 = Pzem-004t

nets:
  3V3: Raspberry_Pi_1.3v3, U1.VCC
  N1: Raspberry_Pi_1.GIPO10, U1.MOSI
  N2: Raspberry_Pi_1.GIPO9, U1.MISO
  N3: Raspberry_Pi_1.GIPO11, U1.SCK
  N4: Raspberry_Pi_1.GIPO19, U1.RST
  N5: Raspberry_Pi_1.GIPO8, U1.NSS
  N6: Raspberry_Pi_1.GIPO15, M1.TX
  N7: Raspberry_Pi_1.GIPO14, M1.RX
  GND: Raspberry_Pi_1.GND, 2_Channel_Relay1.GND, R1.Pin_1, Part1.GND, U1.GND, M1.GND
  5V: Raspberry_Pi_1.5V, 2_Channel_Relay1.VCC#14, Part1.VCC, M1.5V
  N8: 2_Channel_Relay1.JD-VCC, 2_Channel_Relay1.VCC#9

notes:
  5V Power line
  3V3 power line

custom parts:
  2 Channel Power Relay: A 2 channel power relay. The module operates at 5V.
  TXS0108: This 8-bit non-inverting translator uses two separate configurable power-supply rails. The A port tracks the VCCA pin supply voltage. The VCCA pin accepts any supply voltage between 1.2 V and 3.6 V. The B port tracks the VCCB pin supply voltage. The VCCB pin accepts any supply voltage between 1.65 V and 5.5 V. Two input supply pins allows for low Voltage bidirectional translation between any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
  LCD1602-I2C: A standard character display, usually with 2x16 characters. Comes in many colors with LCM1602 IIC attached.
  RFID RC522 SIP - 8 pins: A SIP stand-in part for RFID RC522 . With 8 pins on a 300 mil single inline package (SIP) footprint.
  Pzem-004t: Pzem-004t used for measuring AC voltage, current, active power, frequency, power factor and active energy, the module is without display function, the data is read through the TTL interface.
